# Fritzing sketch FBV_MIDI_schematic (saved by Fritzing 0.9.2b)
breadboards: 1

parts:
  R11 = Resistor [tolerance=±5% resistance=220 package=THT]
  Arduino = Arduino Mega 2560 (Rev3)
  MAX488e_1 = Max488e [chip_label=Max488e package="DIP (Dual Inline) [THT]"]
  RJ-45_(to_FBV) = RJ45 Jack [package=rj45-8]
  9V_Barrel_Jack1 = Power Jack [package=power_jack_pth_lock]
  MIDI_OUT = DIN-5 jack (MIDI) [package=THT]
  R13 = Resistor [tolerance=±5% resistance=220 package=THT]
  MIDI_IN = DIN-5 jack (MIDI) [package=THT]
  R14 = Resistor [tolerance=±5% resistance=220 package=THT]
  4N25 = 4N25 [package=THT]
  D2 = Rectifier Diode [part_number=1N4001 package="300 mil [THT]"]
  R15 = Resistor [tolerance=±5% resistance=1M package=THT]
  R16 = Resistor [tolerance=±5% resistance=3.3k package=THT]
  RJ-45_(optional_to_HD) = RJ45 Jack [package=rj45-8]
  MAX488e_2 = Max488e [chip_label=Max488e package="DIP (Dual Inline) [THT]"]

nets:
  5V: R11.Pin_0, Arduino.5V, MAX488e_1.pin1, R16.Pin_1, MAX488e_2.pin1
  N1: R11.Pin_1, MIDI_OUT.4
  N2: Arduino.D19/RX1, MAX488e_1.pin2
  N3: Arduino.D18/TX1, MAX488e_1.pin3
  N4: Arduino.D17_PWM/RX2, 4N25.Pin_5, R16.Pin_0
  N5: Arduino.D16_PWM/TX2, R13.Pin_0
  N6: Arduino.D15/RX3, MAX488e_2.pin2
  N7: Arduino.D14/TX3, MAX488e_2.pin3
  GND: Arduino.GND, MAX488e_1.pin4, RJ-45_(to_FBV).1, 9V_Barrel_Jack1.PWR, MIDI_OUT.2, 4N25.Pin_4, R15.Pin_1, RJ-45_(optional_to_HD).1, MAX488e_2.pin4
  N8: MAX488e_1.pin5, RJ-45_(to_FBV).7
  N9: MAX488e_1.pin6, RJ-45_(to_FBV).8
  N10: MAX488e_1.pin7, RJ-45_(to_FBV).6
  N11: MAX488e_1.pin8, RJ-45_(to_FBV).3
  N12: RJ-45_(to_FBV).2, 9V_Barrel_Jack1.GND
  9V: 9V_Barrel_Jack1.GNDBREAK
  N13: MIDI_OUT.5, R13.Pin_1
  N14: MIDI_IN.5, 4N25.Pin_2, D2.anode
  N15: MIDI_IN.4, R14.Pin_1
  N16: R14.Pin_0, 4N25.Pin_1, D2.cathode
  N17: 4N25.Pin_6, R15.Pin_0
  N18: RJ-45_(optional_to_HD).3, MAX488e_2.pin5
  N19: RJ-45_(optional_to_HD).6, MAX488e_2.pin6
  N20: RJ-45_(optional_to_HD).7, MAX488e_2.pin8
  N21: RJ-45_(optional_to_HD).8, MAX488e_2.pin7

notes:
  Additional RJ45 optional for Line 6 products as they do not support sysex messages over MIDI. Pinout is:
  1. GND
  2. +7.5-9V
  3. RX-
  4. GND
  5. +7.5-9V
  6. RX+
  7. TX-
  8. TX+
  FBV Pinout:
  1. GND
  2. +7.5-9V
  3. RX-
  4. GND (redundant)
  5. +7.5-9V (redundant)
  6. RX+
  7. TX-
  8. TX+

custom parts:
  4N25: Optocoupler
